# Fritzing sketch Untitled Sketch 2 (saved by Fritzing 0.9.10b)
breadboards: 1

parts:
  TFT_1 = MHS4001
  M1 = Raspberry Pi Pico
  microSD1 = MicroSD Card Module
  M2 = pcf8574 io expansion board [package=THT]
  Bauteil1 = 4x4 Keypad [part_number=101207]

nets:
  VCC: TFT_1.pin_2, TFT_1.pin_4, M1.pin_40, microSD1.VCC, M2.VCC
  GND: TFT_1.pin_6, TFT_1.pin_9, TFT_1.pin_14, TFT_1.pin_20, TFT_1.pin_25, M1.pin_3, M1.pin_8, M1.pin_13, M1.pin_18, M1.pin_23, M1.pin_28, M1.pin_33, M1.pin_38, M1.pin_42, microSD1.GND, M2.GND
  N1: TFT_1.pin_11, M1.pin_31
  N2: TFT_1.pin_18, M1.pin_26
  N3: TFT_1.pin_19, M1.pin_25
  N4: TFT_1.pin_21, M1.pin_21
  N5: TFT_1.pin_22, M1.pin_29
  N6: TFT_1.pin_23, M1.pin_24
  N7: TFT_1.pin_24, M1.pin_22
  N8: TFT_1.pin_26, M1.pin_27
  N9: M1.pin_1, M2.SDA
  N10: M1.pin_2, M2.SCL
  N11: M2.A2+, M2.A2c
  N12: M2.A1+, M2.A1c
  N13: M2.A0+, M2.A0c
  N14: M2.O0, Bauteil1.8
  N15: M2.O1, Bauteil1.7
  N16: M2.O2, Bauteil1.6
  N17: M2.O3, Bauteil1.5
  N18: M2.O4, Bauteil1.4
  N19: M2.O5, Bauteil1.3
  N20: M2.O6, Bauteil1.2
  N21: M2.O7, Bauteil1.1

custom parts:
  MHS4001: Physical resolution 480 x 320, with resistive touch control It supports up to 125MHz SPI signal input, showing stable no screen and no flicker ST7796s XPT2046
  Raspberry Pi Pico: Raspberry Pi Pico. Based around the RP2040 microcontroller the Pico is a low cost microcontroller device bringing Raspberry Pi quality, cost, and easy of use to the microcontroller space. Jan 2021, Split part in to two versions: SMD (this one) and tht. This one is single sided and uses the castellation pads to solder the module to the board (no holes, other than for the USB connector!). The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
  pcf8574 io expansion board: pcf8574 io expansion board.
  4x4 Keypad: Matrix membrane keypad 4x4
